// Logisim project M4_8.1.circ as structural Verilog: 1 circuit, main circuit main
module main (
);

  wire ABUSHL, ABUSPC, ABUSSP, ABUST, and_2_out, and_3_out, and_8_out, CLK, clock_1_out, comparator_1_eq,
       comparator_2_eq, d_ff_2_qn, DBUSA, DBUSB, DBUSH, DBUSL, DBUSPCH, DBUSPCL, DBUSSPH, DBUSSPL, DBUSTL,
       demultiplexer_3_out1, DREAD, DWRITE, HALT, LOADA, LOADB, LOADH, LOADL, LOADPC, LOADSPH, LOADSPL,
       LOADTH, LOADTL, nor_1_out, nor_2_out, nor_3_out, nor_4_out, not_1_out, not_3_out, nPOR, NXTI,
       or_1_out, or_2_out, or_3_out, PCINC, PH0, POR, por_1_out, RAMREAD, RAMWRITE, RUN, RUNNING, SPL_carry,
       SPOP, SPUP, SS, STOP;
  wire [1:1] and_1_out;
  wire [2:0] PH;
  wire [3:0] bit_extender_2_out;
  wire [7:0] A_q, B_q, BOOTROM_data, controlled_buffer_7_out, DATA, H_q, IR, L_q, TL_q;
  wire [15:0] AD, bit_extender_1_out, IDECODE_data, PC, SP;
  wire [15:5] and_7_out;
  wire [15:8] PCDATA16;

  Clock clock_1 (.out(clock_1_out));
  or or_1 (or_1_out, POR, STOP, HALT);
  or or_2 (or_2_out, PH0, PCINC);
  POR #(.PorHighDuration(1), .porsize(1)) por_1 (.out(por_1_out));
  and and_1 (and_1_out[1], clock_1_out, nPOR);
  nor nor_1 (nor_1_out, RUN, nor_2_out);
  nor nor_2 (nor_2_out, nor_1_out, or_1_out);
  Counter #(.max('hffff), .width(16)) u_PC (
    .clr(POR), .load(LOADPC), .count(or_2_out), .clk(CLK), .D({PCDATA16, DATA}), .Q(PC));  // open: up, carry
  D_Flip_Flop d_ff_1 (.D(nor_2_out), .clk(clock_1_out), .Q(RUNNING));  // open: Qn, preset, reset
  Counter SPL (.clr(POR), .load(LOADSPL), .up(SPUP), .count(SPOP), .clk(CLK), .D(DATA), .carry(SPL_carry), .Q(SP[7:0]));
  nor nor_3 (nor_3_out, AD[15], AD[14], AD[13], AD[12], AD[11], AD[10]);
  ROM #(.addrWidth(10)) BOOTROM (.addr(AD[9:0]), .data(BOOTROM_data));
  D_Flip_Flop #(.trigger("falling")) d_ff_2 (
    .D(not_1_out), .clk(clock_1_out), .Qn(d_ff_2_qn));  // open: Q, preset, reset
  not not_1 (not_1_out, por_1_out);
  BitSelector #(.width(2)) bitselector_1 (.in({and_1_out[1], SS}), .out(CLK), .sel(RUNNING));
  Counter #(.max('h7), .width(3)) PHASECOUNTER (
    .clr(POR), .load(NXTI), .clk(CLK), .D(3'b000), .Q(PH));  // open: up, count, carry
  assign AD = or_3_out ? PC : 16'bz;  // Controlled_Buffer controlled_buffer_1
  or or_3 (or_3_out, PH0, ABUSPC);
  or or_4 (POR, por_1_out, d_ff_2_qn);
  assign DATA = DBUSPCL ? PC[7:0] : 8'bz;  // Controlled_Buffer controlled_buffer_2
  assign DATA = DBUSPCH ? PC[15:8] : 8'bz;  // Controlled_Buffer controlled_buffer_3
  and and_2 (and_2_out, SPOP, SPL_carry);
  not not_2 (nPOR, POR);
  Counter counter_1 (
    .clr(POR), .load(LOADSPH), .up(SPUP), .count(and_2_out), .clk(CLK), .D(DATA), .Q(SP[15:8]));  // open: carry
  and and_3 (and_3_out, nor_3_out, DREAD);
  assign DATA = and_3_out ? BOOTROM_data : 8'bz;  // Controlled_Buffer controlled_buffer_4
  nor nor_4 (nor_4_out, PH[0], PH[1], PH[2]);
  Register u_IR (.D(DATA), .en(PH0), .clk(CLK), .Q(IR), .clr(POR));
  and and_4 (PH0, nPOR, nor_4_out);
  RAM #(.addrWidth(10), .asyncread("true"), .databus("bidir"), .\type ("nonvolatile")) ram_1 (
    .addr(AD[9:0]), .we(RAMWRITE), .oe(RAMREAD), .clk(CLK));  // open: data
  LED led_1 (.in(RUNNING));
  LED led_2 (.in(POR));
  assign AD = ABUSSP ? SP : 16'bz;  // Controlled_Buffer controlled_buffer_5
  Comparator #(.width(6)) comparator_1 (.a({6{1'b1}}), .b(AD[15:10]), .eq(comparator_1_eq));  // open: gt, lt
  LED led_3 (.in(CLK));
  Hex_Digit_Display hex_digit_display_1 (.value(PC[15:12]));  // open: dp
  Button button_1 (.out(RUN));
  ROM #(.addrWidth(11), .dataWidth(16)) IDECODE (.addr({IR, PH}), .data(IDECODE_data));
  Hex_Digit_Display hex_digit_display_2 (.value(PC[11:8]));  // open: dp
  Hex_Digit_Display hex_digit_display_3 (.value(PC[7:4]));  // open: dp
  Button button_2 (.out(STOP));
  and and_5 (RAMREAD, DREAD, comparator_1_eq);
  and and_6 (RAMWRITE, comparator_1_eq, DWRITE);
  Hex_Digit_Display hex_digit_display_4 (.value(PC[3:0]));  // open: dp
  Button button_3 (.out(SS));
  assign DATA = RAMREAD ? controlled_buffer_7_out : 8'bz;  // Controlled_Buffer controlled_buffer_6
  assign controlled_buffer_7_out = RAMWRITE ? DATA : 8'bz;  // Controlled_Buffer controlled_buffer_7
  Hex_Digit_Display hex_digit_display_5 (.value(IR[7:4]));  // open: dp
  Hex_Digit_Display hex_digit_display_6 (.value(IR[3:0]));  // open: dp
  assign bit_extender_1_out = {{15{PH0}}, PH0};  // Bit_Extender bit_extender_1
  Hex_Digit_Display hex_digit_display_7 (.value(bit_extender_2_out));  // open: dp
  assign bit_extender_2_out = {{1{1'b0}}, PH};  // Bit_Extender bit_extender_2
  assign {and_7_out, SPUP, SPOP, HALT, PCINC, NXTI} = IDECODE_data & ~bit_extender_1_out;  // AND_Gate and_7, 16 bits wide
  Hex_Digit_Display hex_digit_display_8 (.value(DATA[7:4]));  // open: dp
  Hex_Digit_Display hex_digit_display_9 (.value(DATA[3:0]));  // open: dp
  Register A (.D(DATA), .en(LOADA), .clk(CLK), .Q(A_q));  // open: clr
  Register B (.D(DATA), .en(LOADB), .clk(CLK), .Q(B_q));  // open: clr
  Register H (.D(DATA), .en(LOADH), .clk(CLK), .Q(H_q));  // open: clr
  Register L (.D(DATA), .en(LOADL), .clk(CLK), .Q(L_q));  // open: clr
  not not_3 (not_3_out, PH0);
  Demultiplexer #(.select(3)) demultiplexer_1 (
    .out1(ABUSPC), .out2(ABUSSP), .out3(ABUSHL), .out4(ABUST), .in(not_3_out), .sel(and_7_out[7:5]));  // open: out0, out5, out6, out7
  Demultiplexer #(.select(4)) demultiplexer_2 (
    .out1(DWRITE), .out2(LOADPC), .out3(LOADSPH), .out4(LOADSPL), .out5(LOADTH), .out6(LOADTL), .out7(LOADA),
    .out8(LOADB), .out9(LOADH), .out10(LOADL), .in(not_3_out), .sel(and_7_out[11:8]));  // open: out0, out11, out12, out13, out14, out15
  Demultiplexer #(.select(4)) demultiplexer_3 (
    .out1(demultiplexer_3_out1), .out2(DBUSPCH), .out3(DBUSPCL), .out4(DBUSSPH), .out5(DBUSSPL),
    .out6(DBUSTL), .out7(DBUSA), .out8(DBUSB), .out9(DBUSH), .out10(DBUSL), .in(not_3_out),
    .sel(and_7_out[15:12]));  // open: out0, out11, out12, out13, out14, out15
  assign DATA = DBUSA ? A_q : 8'bz;  // Controlled_Buffer controlled_buffer_8
  assign DATA = DBUSB ? B_q : 8'bz;  // Controlled_Buffer controlled_buffer_9
  assign DATA = DBUSH ? H_q : 8'bz;  // Controlled_Buffer controlled_buffer_10
  assign AD = ABUSHL ? {H_q, L_q} : 16'bz;  // Controlled_Buffer controlled_buffer_11
  assign DATA = DBUSL ? L_q : 8'bz;  // Controlled_Buffer controlled_buffer_12
  TTY tty_1 (.data(DATA[6:0]), .clk(CLK), .we(and_8_out));  // open: clr
  or or_5 (DREAD, PH0, demultiplexer_3_out1);
  and and_8 (and_8_out, comparator_2_eq, DWRITE);
  Comparator #(.width(16)) comparator_2 (.a(16'h400), .b(AD), .eq(comparator_2_eq));  // open: gt, lt
  Register TL (.D(DATA), .en(LOADTL), .clk(CLK), .Q(TL_q));  // open: clr
  Register TH (.D(DATA), .en(LOADTH), .clk(CLK), .Q(PCDATA16));  // open: clr
  assign DATA = DBUSTL ? TL_q : 8'bz;  // Controlled_Buffer controlled_buffer_13
  assign AD = ABUST ? {PCDATA16, TL_q} : 16'bz;  // Controlled_Buffer controlled_buffer_14

  // Other names for the same wires on the sheet: PCDATA16[7:0] = DATA

  // Notes on the sheet:
  //   contents of BOOTROM (hex, n*v repeats v):
  //   ff 48 4 4 0 0 65 4 4 0 0 6c 4 4 0 0 6c 4 4 0 0 6f 4 4 0 0 20 4 4 0 0 77 4 4 0 0 6f 4 4 0 0 72 4 4 0
  //   0 6c 4 4 0 0 64 4 4 0 0 21 4 4 0 0 a 4 4 0 ff
  //   RUN
  //   RST
  //   CLK
  //   contents of IDECODE (hex, n*v repeats v):
  //   0 1723 7*0 1823 7*0 1923 7*0 1a23 7*0 1522 1622 7181 93*0 7801 127*0 1322 1423 766*0 1522 1221 6*0
  //   1522 1622 2148 3148 6201 0 0 0 18 1658 1540 6201 996*0 5
  //   PC
  //   IR
  //   PH
endmodule
